// Logisim project Sahitaj_Gerber_labo_alu.circ as structural Verilog: 9 circuits, main circuit ALU_MAXV
module ALU_MAXV (
  input  [3:0] a_i,
  input  [3:0] b_i,
  output [3:0] c_o,
  output erreur_o
);

  wire [5:0] opcode_i_sw6;

  DipSwitch opcode_i (
    .sw1(opcode_i_sw6[5]), .sw2(opcode_i_sw6[4]), .sw3(opcode_i_sw6[3]), .sw4(opcode_i_sw6[2]),
    .sw5(opcode_i_sw6[1]), .sw6(opcode_i_sw6[0]));  // open: sw7, sw8
  ALU_Top alu_inst (.a_i(a_i), .b_i(b_i), .op_i(opcode_i_sw6), .c_o(c_o), .erreur_o(erreur_o));

  // Notes on the sheet:
  //   Attention, votre version de Logisim
  //   ne contient pas de tracker. Si vous
  //   enregistrez votre projet, toutes les
  //   informations du tracker seront
  //   définitivement effacées.
endmodule

module ALU_Top (
  input  [3:0] a_i,
  input  [3:0] b_i,
  input  [5:0] op_i,
  output [3:0] c_o,
  output erreur_o
);

  wire ALU_AddSub4bit_A_carry_o, ALU_AddSub4bit_A_negative_o, ALU_AddSub4bit_A_overflow_o,
       ALU_AddSub4bit_A_zero_o;
  wire [3:0] ALU_AddSub4bit_A_r_o, ALU_Comparator_A_cmp_o, ALU_Custom_A_s_o, ALU_LogicUnit_A_f_o;

  ALU_Custom ALU_Custom_A (.a_i(a_i), .s_o(ALU_Custom_A_s_o));
  ALU_AddSub4bit ALU_AddSub4bit_A (
    .a_i(a_i), .b_i(b_i), .op_i(op_i[3:2]), .r_o(ALU_AddSub4bit_A_r_o), .carry_o(ALU_AddSub4bit_A_carry_o),
    .zero_o(ALU_AddSub4bit_A_zero_o), .overflow_o(ALU_AddSub4bit_A_overflow_o),
    .negative_o(ALU_AddSub4bit_A_negative_o));
  ALU_Comparator ALU_Comparator_A (
    .negative_i(ALU_AddSub4bit_A_negative_o), .zero_i(ALU_AddSub4bit_A_zero_o),
    .carry_i(ALU_AddSub4bit_A_carry_o), .op_i(op_i[2:0]), .cmp_o(ALU_Comparator_A_cmp_o));
  ALU_LogicUnit ALU_LogicUnit_A (.a_i(a_i), .b_i(b_i), .op_i(op_i[5:4]), .f_o(ALU_LogicUnit_A_f_o));
  Multiplexer #(.select(2), .width(4), .enable("false")) multiplexer_1 (
    .in0(ALU_AddSub4bit_A_r_o), .in1(ALU_Comparator_A_cmp_o), .in2(ALU_LogicUnit_A_f_o),
    .in3(ALU_Custom_A_s_o), .out(c_o), .sel(op_i[5:4]));
  ALU_Error ALU_Error_A (
    .op_msb_i(op_i[5:4]), .overflow_i(ALU_AddSub4bit_A_overflow_o), .op_i(op_i[3:0]), .error_o(erreur_o));

  // Notes on the sheet:
  //   Attention, votre version de Logisim
  //   ne contient pas de tracker. Si vous
  //   enregistrez votre projet, toutes les
  //   informations du tracker seront
  //   définitivement effacées.
endmodule

module Add1bit (
  input  a_i,
  input  b_i,
  input  c_i,
  output r_o,
  output c_o
);

  wire and_1_out, and_2_out, and_3_out, xor_1_out;

  xor xor_1 (xor_1_out, a_i, b_i);
  and and_1 (and_1_out, a_i, b_i);
  and and_2 (and_2_out, a_i, c_i);
  and and_3 (and_3_out, b_i, c_i);
  xor xor_2 (r_o, xor_1_out, c_i);
  or or_1 (c_o, and_1_out, and_2_out, and_3_out);

  // Notes on the sheet:
  //   Attention, votre version de Logisim
  //   ne contient pas de tracker. Si vous
  //   enregistrez votre projet, toutes les
  //   informations du tracker seront
  //   définitivement effacées.
endmodule

module Add4bit (
  input  c_i,
  input  [3:0] a_i,
  input  [3:0] b_i,
  output [3:0] r_o,
  output c_o
);

  wire Add1bit_A_c_o, Add1bit_B_c_o, Add1bit_C_c_o;

  Add1bit Add1bit_A (.a_i(a_i[0]), .b_i(b_i[0]), .c_i(c_i), .r_o(r_o[0]), .c_o(Add1bit_A_c_o));
  Add1bit Add1bit_B (.a_i(a_i[1]), .b_i(b_i[1]), .c_i(Add1bit_A_c_o), .r_o(r_o[1]), .c_o(Add1bit_B_c_o));
  Add1bit Add1bit_C (.a_i(a_i[2]), .b_i(b_i[2]), .c_i(Add1bit_B_c_o), .r_o(r_o[2]), .c_o(Add1bit_C_c_o));
  Add1bit Add1bit_D (.a_i(a_i[3]), .b_i(b_i[3]), .c_i(Add1bit_C_c_o), .r_o(r_o[3]), .c_o(c_o));

  // Notes on the sheet:
  //   Attention, votre version de Logisim
  //   ne contient pas de tracker. Si vous
  //   enregistrez votre projet, toutes les
  //   informations du tracker seront
  //   définitivement effacées.
endmodule

module ALU_AddSub4bit (
  input  [3:0] a_i,
  input  [3:0] b_i,
  input  [1:0] op_i,
  output [3:0] r_o,
  output carry_o,
  output zero_o,
  output overflow_o,
  output negative_o
);

  wire and_2_out, and_3_out, or_1_out, xor_5_out, xor_6_out;
  wire [3:0] xor_1_out;

  xor xor_1 (xor_1_out[0], b_i[0], op_i[1]);
  xor xor_2 (xor_1_out[1], b_i[1], op_i[1]);
  xor xor_3 (xor_1_out[2], b_i[2], op_i[1]);
  xor xor_4 (xor_1_out[3], b_i[3], op_i[1]);
  Add4bit Add4bit_A (.c_i(op_i[1]), .a_i(a_i), .b_i(xor_1_out), .r_o(r_o), .c_o(carry_o));
  xor xor_5 (xor_5_out, carry_o, op_i[1]);
  xor xor_6 (xor_6_out, r_o[3], overflow_o);
  nor nor_1 (zero_o, r_o[0], r_o[1], r_o[2], r_o[3]);
  and and_1 (negative_o, xor_6_out, ~op_i[0]);  // AND_Gate
  and and_2 (and_2_out, a_i[3], xor_1_out[3], ~r_o[3]);  // AND_Gate
  and and_3 (and_3_out, ~a_i[3], ~xor_1_out[3], r_o[3]);  // AND_Gate
  or or_1 (or_1_out, and_2_out, and_3_out);
  Multiplexer #(.enable("false")) multiplexer_1 (.in0(or_1_out), .in1(xor_5_out), .out(overflow_o), .sel(op_i[0]));

  // Notes on the sheet:
  //   Attention, votre version de Logisim
  //   ne contient pas de tracker. Si vous
  //   enregistrez votre projet, toutes les
  //   informations du tracker seront
  //   définitivement effacées.
endmodule

module ALU_Comparator (
  input  negative_i,
  input  zero_i,
  input  carry_i,
  input  [2:0] op_i,
  output [3:0] cmp_o
);

  wire not_1_out, not_2_out, not_3_out;

  not not_1 (not_1_out, negative_i);
  not not_2 (not_2_out, zero_i);
  not not_3 (not_3_out, carry_i);
  Multiplexer #(.select(3), .enable("false")) multiplexer_1 (
    .in0(1'b0), .in1(not_1_out), .in2(negative_i), .in3(not_2_out), .in4(zero_i), .in5(carry_i),
    .in6(not_3_out), .in7(1'b0), .out(cmp_o[0]), .sel(op_i));

  assign cmp_o[3:1] = 3'b000;

  // Notes on the sheet:
  //   Attention, votre version de Logisim
  //   ne contient pas de tracker. Si vous
  //   enregistrez votre projet, toutes les
  //   informations du tracker seront
  //   définitivement effacées.
endmodule

module ALU_LogicUnit (
  input  [3:0] a_i,
  input  [3:0] b_i,
  input  [1:0] op_i,
  output [3:0] f_o
);

  wire [3:0] and_1_out, nand_1_out, or_1_out, xor_1_out;

  assign and_1_out = a_i & b_i;  // AND_Gate and_1, 4 bits wide
  assign or_1_out = a_i | b_i;  // OR_Gate or_1, 4 bits wide
  assign nand_1_out = ~(a_i & b_i);  // NAND_Gate nand_1, 4 bits wide
  assign xor_1_out = a_i ^ b_i;  // XOR_Gate xor_1, 4 bits wide
  Multiplexer #(.select(2), .width(4), .enable("false")) multiplexer_1 (
    .in0(and_1_out), .in1(or_1_out), .in2(nand_1_out), .in3(xor_1_out), .out(f_o), .sel(op_i));

  // Notes on the sheet:
  //   Attention, votre version de Logisim
  //   ne contient pas de tracker. Si vous
  //   enregistrez votre projet, toutes les
  //   informations du tracker seront
  //   définitivement effacées.
endmodule

module ALU_Custom (
  input  [3:0] a_i,
  output [3:0] s_o
);

  ExactlyOne xor_1 (.out(s_o[0]), .in0(a_i[0]), .in1(a_i[1]), .in2(a_i[2]), .in3(a_i[3]));

  assign s_o[3:1] = 3'b000;

  // Notes on the sheet:
  //   Attention, votre version de Logisim
  //   ne contient pas de tracker. Si vous
  //   enregistrez votre projet, toutes les
  //   informations du tracker seront
  //   définitivement effacées.
endmodule

module ALU_Error (
  input  [1:0] op_msb_i,
  input  overflow_i,
  input  [3:0] op_i,
  output error_o
);

  wire and_1_out, and_2_out, or_1_out;

  and and_1 (and_1_out, op_i[0], op_i[1], op_i[2]);
  and and_2 (and_2_out, ~op_i[0], ~op_i[1], ~op_i[2]);  // AND_Gate
  or or_1 (or_1_out, and_1_out, and_2_out, ~op_i[3]);  // OR_Gate
  Multiplexer #(.select(2), .enable("false")) multiplexer_1 (
    .in0(overflow_i), .in1(or_1_out), .in2(1'b0), .in3(1'b0), .out(error_o), .sel(op_msb_i));

  // Notes on the sheet:
  //   Attention, votre version de Logisim
  //   ne contient pas de tracker. Si vous
  //   enregistrez votre projet, toutes les
  //   informations du tracker seront
  //   définitivement effacées.
endmodule
