// Logisim project Sahitaj_Cornu_labo_chenillard_etu.circ as structural Verilog: 6 circuits, main circuit MAXV_CHENILLARD
module MAXV_CHENILLARD (
  input  [7:0] switch_i,
  input  load_i,
  input  clk_i,
  input  nReset_i,
  output [7:0] led_o
);

  wire entree_i_sw7, entree_i_sw8, not_1_out;
  wire [1:0] entree_i_sw2;

  DipSwitch entree_i (
    .sw1(entree_i_sw2[1]), .sw2(entree_i_sw2[0]), .sw7(entree_i_sw7), .sw8(entree_i_sw8));  // open: sw3, sw4, sw5, sw6
  not not_1 (not_1_out, nReset_i);
  chenillard_TOP chenillard_TOP_A (
    .val_i(switch_i), .right_nleft_i(entree_i_sw8), .load_i(load_i), .enable_i(entree_i_sw7),
    .speed_i(entree_i_sw2), .clk_i(clk_i), .reset_i(not_1_out), .led_o(led_o));

  // Notes on the sheet:
  //   Attention, votre version de Logisim
  //   ne contient pas de tracker. Si vous
  //   enregistrez votre projet, toutes les
  //   informations du tracker seront
  //   définitivement effacées.
endmodule

module chenillard_TOP (
  input  [7:0] val_i,
  input  right_nleft_i,
  input  load_i,
  input  enable_i,
  input  [1:0] speed_i,
  input  clk_i,
  input  reset_i,
  output [7:0] led_o
);

  wire timer_28b_A_done_o;
  wire [1:0] multiplexer_2_out, multiplexer_3_out;
  wire [27:0] multiplexer_1_out;

  Multiplexer #(.select(2), .width(28), .enable("false")) multiplexer_1 (
    .in0(28'h7270e0), .in1(28'he4e1c0), .in2(28'h1c9c380), .in3(28'h3937800), .out(multiplexer_1_out),
    .sel(speed_i));
  timer_28b timer_28b_A (
    .value_i(multiplexer_1_out), .en_i(enable_i), .load_i(load_i), .clk_i(clk_i), .reset_i(reset_i),
    .done_o(timer_28b_A_done_o));
  Multiplexer #(.width(2)) multiplexer_2 (
    .in0({1'b1, right_nleft_i}), .in1(2'b00), .out(multiplexer_2_out), .sel(timer_28b_A_done_o), .en(enable_i));
  Multiplexer #(.width(2), .enable("false")) multiplexer_3 (
    .in0(multiplexer_2_out), .in1(2'b01), .out(multiplexer_3_out), .sel(load_i));
  shift_reg_8b shift_reg_8b_A (
    .ser_l_i(led_o[0]), .value_load_i(val_i), .mode_i(multiplexer_3_out), .ser_r_i(led_o[7]), .clk_i(clk_i),
    .reset_i(reset_i), .val_o(led_o));

  // Notes on the sheet:
  //   Attention, votre version de Logisim
  //   ne contient pas de tracker. Si vous
  //   enregistrez votre projet, toutes les
  //   informations du tracker seront
  //   définitivement effacées.
endmodule

module shift_reg_4b (
  input  ser_l_i,
  input  ser_r_i,
  input  [3:0] value_load_i,
  input  [1:0] mode_i,
  input  clk_i,
  input  reset_i,
  output [3:0] val_o
);

  wire multiplexer_1_out, multiplexer_2_out, multiplexer_3_out, multiplexer_4_out;

  Multiplexer #(.select(2), .enable("false")) multiplexer_1 (
    .in0(val_o[3]), .in1(value_load_i[3]), .in2(val_o[2]), .in3(ser_r_i), .out(multiplexer_1_out),
    .sel(mode_i));
  D_Flip_Flop d_ff_1 (.D(multiplexer_1_out), .clk(clk_i), .Q(val_o[3]), .preset(1'b0), .reset(reset_i));  // open: Qn
  Multiplexer #(.select(2), .enable("false")) multiplexer_2 (
    .in0(val_o[2]), .in1(value_load_i[2]), .in2(val_o[1]), .in3(val_o[3]), .out(multiplexer_2_out),
    .sel(mode_i));
  D_Flip_Flop d_ff_2 (.D(multiplexer_2_out), .clk(clk_i), .Q(val_o[2]), .preset(1'b0), .reset(reset_i));  // open: Qn
  Multiplexer #(.select(2), .enable("false")) multiplexer_3 (
    .in0(val_o[1]), .in1(value_load_i[1]), .in2(val_o[0]), .in3(val_o[2]), .out(multiplexer_3_out),
    .sel(mode_i));
  D_Flip_Flop d_ff_3 (.D(multiplexer_3_out), .clk(clk_i), .Q(val_o[1]), .preset(1'b0), .reset(reset_i));  // open: Qn
  Multiplexer #(.select(2), .enable("false")) multiplexer_4 (
    .in0(val_o[0]), .in1(value_load_i[0]), .in2(ser_l_i), .in3(val_o[1]), .out(multiplexer_4_out),
    .sel(mode_i));
  D_Flip_Flop d_ff_4 (.D(multiplexer_4_out), .clk(clk_i), .Q(val_o[0]), .preset(1'b0), .reset(reset_i));  // open: Qn

  // Notes on the sheet:
  //   Attention, votre version de Logisim
  //   ne contient pas de tracker. Si vous
  //   enregistrez votre projet, toutes les
  //   informations du tracker seront
  //   définitivement effacées.
endmodule

module shift_reg_8b (
  input  ser_l_i,
  input  [7:0] value_load_i,
  input  [1:0] mode_i,
  input  ser_r_i,
  input  clk_i,
  input  reset_i,
  output [7:0] val_o
);

  shift_reg_4b shift_reg_4b_A (
    .ser_l_i(val_o[3]), .ser_r_i(ser_l_i), .value_load_i(value_load_i[7:4]), .mode_i(mode_i), .clk_i(clk_i),
    .reset_i(reset_i), .val_o(val_o[7:4]));
  shift_reg_4b shift_reg_4b_B (
    .ser_l_i(ser_r_i), .ser_r_i(val_o[4]), .value_load_i(value_load_i[3:0]), .mode_i(mode_i), .clk_i(clk_i),
    .reset_i(reset_i), .val_o(val_o[3:0]));

  // Notes on the sheet:
  //   Attention, votre version de Logisim
  //   ne contient pas de tracker. Si vous
  //   enregistrez votre projet, toutes les
  //   informations du tracker seront
  //   définitivement effacées.
endmodule

module timer_28b (
  input  [27:0] value_i,
  input  en_i,
  input  load_i,
  input  clk_i,
  input  reset_i,
  output done_o
);

  wire or_1_out;
  wire [27:0] multiplexer_1_out, register_1_q, subtractor_1_out;

  Subtractor #(.width(28)) subtractor_1 (
    .a(register_1_q), .b({28{1'b0}}), .out(subtractor_1_out), .bin(1'b1));  // open: bout
  or or_1 (or_1_out, load_i, done_o);
  Register #(.width(28)) register_1 (.D(multiplexer_1_out), .en(en_i), .clk(clk_i), .Q(register_1_q), .clr(reset_i));
  Multiplexer #(.width(28), .enable("false")) multiplexer_1 (
    .in0(subtractor_1_out), .in1(value_i), .out(multiplexer_1_out), .sel(or_1_out));
  Comparator #(.width(28)) comparator_1 (.a(register_1_q), .b({28{1'b0}}), .eq(done_o));  // open: gt, lt

  // Notes on the sheet:
  //   Attention, votre version de Logisim
  //   ne contient pas de tracker. Si vous
  //   enregistrez votre projet, toutes les
  //   informations du tracker seront
  //   définitivement effacées.
endmodule

module chronogramme (
  input  [7:0] val_i,
  input  right_nleft_i,
  input  load_i,
  input  enable_i,
  input  [1:0] speed_i,
  input  reset_i,
  output [7:0] led_o
);

  wire clk_i_out;

  Clock #(.highDuration(4), .lowDuration(4)) sysclk ();  // open: out
  Clock #(.highDuration(4), .lowDuration(4)) clk_i (.out(clk_i_out));
  chenillard_TOP Chenillard_TOP_A (
    .val_i(val_i), .right_nleft_i(right_nleft_i), .load_i(load_i), .enable_i(enable_i), .speed_i(speed_i),
    .clk_i(clk_i_out), .reset_i(reset_i), .led_o(led_o));

  // Notes on the sheet:
  //   Attention, votre version de Logisim
  //   ne contient pas de tracker. Si vous
  //   enregistrez votre projet, toutes les
  //   informations du tracker seront
  //   définitivement effacées.
endmodule
