// Logisim project auto_arm_proj.circ as structural Verilog: 4 circuits, main circuit auto_arm_simulation
module auto_arm_simulation (
);

  wire auto_arm_top_A_dest_blue_o, auto_arm_top_A_dest_init_o, auto_arm_top_A_dest_red_o,
       auto_arm_top_A_drop_o, auto_arm_top_A_move_o, auto_arm_top_A_scan_o, auto_arm_top_A_throw_o,
       clk_i_out, tclconsolereds_1_p23, tclconsolereds_1_p26;
  wire [1:0] tclconsolereds_1_p24;

  Clock clk_i (.out(clk_i_out));
  Clock sysclk ();  // open: out
  auto_arm_top auto_arm_top_A (
    .ready_i(tclconsolereds_1_p23), .color_i(tclconsolereds_1_p24), .clk_i(clk_i_out),
    .reset_i(tclconsolereds_1_p26), .scan_o(auto_arm_top_A_scan_o), .throw_o(auto_arm_top_A_throw_o),
    .move_o(auto_arm_top_A_move_o), .dest_red_o(auto_arm_top_A_dest_red_o),
    .dest_blue_o(auto_arm_top_A_dest_blue_o), .dest_init_o(auto_arm_top_A_dest_init_o),
    .drop_o(auto_arm_top_A_drop_o));
  // TclConsoleReds #(.filePath("console/console_auto_arm.tcl")) tclconsolereds_1: pin names not known; wires that end beside it: 4'b0000, 4'b0000, auto_arm_top_A_scan_o, auto_arm_top_A_throw_o, auto_arm_top_A_move_o, auto_arm_top_A_dest_red_o, auto_arm_top_A_dest_blue_o, auto_arm_top_A_dest_init_o, auto_arm_top_A_drop_o, 1'b0, 1'b0, 1'b0, 1'b0, 1'b0, 1'b0, 1'b0, 1'b0, 1'b0, {16{1'b0}}, {16{1'b0}}, {8{1'b0}}, clk_i_out, tclconsolereds_1_p23, tclconsolereds_1_p24[0], tclconsolereds_1_p24[1], tclconsolereds_1_p26

  // Notes on the sheet:
  //   Attention, votre version de Logisim
  //   ne contient pas de tracker. Si vous
  //   enregistrez votre projet, toutes les
  //   informations du tracker seront
  //   définitivement effacées.
endmodule

module auto_arm_top (
  input  ready_i,
  input  [1:0] color_i,
  input  clk_i,
  input  reset_i,
  output scan_o,
  output throw_o,
  output move_o,
  output dest_red_o,
  output dest_blue_o,
  output dest_init_o,
  output drop_o
);

  wire timer;

  auto_arm auto_arm_A (
    .ready_i(ready_i), .color_i(color_i), .timer_i(timer), .reset_i(reset_i), .drop_o(drop_o),
    .dest_init_o(dest_init_o), .dest_blue_o(dest_blue_o), .dest_red_o(dest_red_o), .move_o(move_o),
    .throw_o(throw_o), .scan_o(scan_o));
  auto_arm_timer auto_arm_timer_A (.en_i(move_o), .reset_i(reset_i), .clk_i(clk_i), .timer_o(timer));

  // Other names for the same wires on the sheet: color[1:0] = color_i; dest_blue = dest_blue_o;
  //   dest_init = dest_init_o; dest_red = dest_red_o; drop = drop_o; move = move_o; ready = ready_i; reset = reset_i

  // Notes on the sheet:
  //   Attention, votre version de Logisim
  //   ne contient pas de tracker. Si vous
  //   enregistrez votre projet, toutes les
  //   informations du tracker seront
  //   définitivement effacées.
endmodule

module auto_arm (
  input  ready_i,
  input  [1:0] color_i,
  input  timer_i,
  input  reset_i,
  output drop_o,
  output dest_init_o,
  output dest_blue_o,
  output dest_red_o,
  output move_o,
  output throw_o,
  output scan_o
);

  wire and_1_out, and_2_out, and_3_out, and_4_out, and_5_out, and_6_out, and_7_out, and_8_out, and_9_out,
       and_10_out, and_11_out, and_12_out, and_13_out, clk_i_out, E0, or_1_out, or_2_out, or_3_out, or_5_out,
       or_6_out, or_7_out;

  Clock clk_i (.out(clk_i_out));
  and and_1 (and_1_out, E0, ~ready_i);  // AND_Gate
  and and_2 (and_2_out, dest_init_o, timer_i);
  or or_1 (or_1_out, throw_o, and_2_out, and_1_out);
  D_Flip_Flop d_ff_1 (.D(or_1_out), .clk(clk_i_out), .Q(E0), .preset(reset_i));  // open: Qn, reset
  and and_3 (and_3_out, E0, ready_i);
  and and_4 (and_4_out, scan_o, color_i[1], color_i[0], ready_i);
  or or_2 (or_2_out, and_3_out, and_4_out);
  D_Flip_Flop d_ff_2 (.D(or_2_out), .clk(clk_i_out), .Q(scan_o), .preset(1'b0), .reset(reset_i));  // open: Qn
  and and_5 (and_5_out, scan_o, ~color_i[1], ~color_i[0], ready_i);  // AND_Gate
  D_Flip_Flop d_ff_3 (.D(and_5_out), .clk(clk_i_out), .Q(throw_o), .preset(1'b0), .reset(reset_i));  // open: Qn
  and and_6 (and_6_out, scan_o, ~color_i[1], color_i[0], ready_i);  // AND_Gate
  and and_7 (and_7_out, dest_red_o, ~timer_i);  // AND_Gate
  or or_3 (or_3_out, and_6_out, and_7_out);
  D_Flip_Flop d_ff_4 (.D(or_3_out), .clk(clk_i_out), .Q(dest_red_o), .preset(1'b0), .reset(reset_i));  // open: Qn
  or or_4 (move_o, dest_red_o, dest_blue_o, dest_init_o);
  and and_8 (and_8_out, dest_blue_o, ~timer_i);  // AND_Gate
  and and_9 (and_9_out, scan_o, color_i[1], ~color_i[0], ready_i);  // AND_Gate
  or or_5 (or_5_out, and_9_out, and_8_out);
  D_Flip_Flop d_ff_5 (.D(or_5_out), .clk(clk_i_out), .Q(dest_blue_o), .preset(1'b0), .reset(reset_i));  // open: Qn
  and and_10 (and_10_out, dest_blue_o, timer_i);
  and and_11 (and_11_out, dest_red_o, timer_i);
  or or_6 (or_6_out, and_11_out, and_10_out);
  D_Flip_Flop d_ff_6 (.D(or_6_out), .clk(clk_i_out), .Q(drop_o), .preset(1'b0), .reset(reset_i));  // open: Qn
  and and_12 (and_12_out, dest_init_o, ~timer_i);  // AND_Gate
  and and_13 (and_13_out, drop_o, ~timer_i);  // AND_Gate
  or or_7 (or_7_out, and_13_out, and_12_out);
  D_Flip_Flop d_ff_7 (.D(or_7_out), .clk(clk_i_out), .Q(dest_init_o), .preset(1'b0), .reset(reset_i));  // open: Qn

  // Other names for the same wires on the sheet: color1 = color_i[0]; color2 = color_i[1]; E1 = scan_o; E2 = throw_o;
  //   E3 = dest_red_o; E4 = dest_blue_o; E5 = drop_o; E6 = dest_init_o; ready = ready_i; timer = timer_i

  // Notes on the sheet:
  //   Attention, votre version de Logisim
  //   ne contient pas de tracker. Si vous
  //   enregistrez votre projet, toutes les
  //   informations du tracker seront
  //   définitivement effacées.
endmodule

module auto_arm_timer (
  input  en_i,
  input  reset_i,
  input  clk_i,
  output timer_o
);

  wire comparator_2_eq, or_1_out;
  wire [1:0] adder_1_out, multiplexer_1_out, register_1_q;

  Adder #(.width(2)) adder_1 (.a(register_1_q), .b(2'b01), .out(adder_1_out), .cin(1'b0));  // open: cout
  Register #(.width(2)) register_1 (.D(multiplexer_1_out), .en(en_i), .clk(clk_i), .Q(register_1_q), .clr(or_1_out));
  Multiplexer #(.width(2), .enable("false")) multiplexer_1 (
    .in0(2'b00), .in1(adder_1_out), .out(multiplexer_1_out), .sel(en_i));
  or or_1 (or_1_out, reset_i, comparator_2_eq);
  Comparator #(.width(2)) comparator_1 (.a(register_1_q), .b(2'b10), .eq(timer_o));  // open: gt, lt
  Comparator #(.width(2)) comparator_2 (.a(register_1_q), .b(2'b11), .eq(comparator_2_eq));  // open: gt, lt

  // Notes on the sheet:
  //   Attention, votre version de Logisim
  //   ne contient pas de tracker. Si vous
  //   enregistrez votre projet, toutes les
  //   informations du tracker seront
  //   définitivement effacées.
endmodule
